// Logisim project loendur.circ as structural Verilog: 3 circuits, main circuit main
module main (
  input  in_1,
  input  in_2,
  output out_3,
  output out_4,
  output out_5,
  output out_6,
  output out_7,
  output out_8,
  output out_9,
  output out_10
);

  Hex_Digit_Display hex_digit_display_1 (.value({out_6, out_5, out_4, out_3}));  // open: dp
  T_Flip_Flop t_ff_1 (.clk(in_1), .T(in_2), .Q(out_3), .Qn(out_10));  // open: preset, reset, en
  T_Flip_Flop t_ff_2 (.clk(out_3), .T(in_2), .Q(out_4), .Qn(out_9));  // open: preset, reset, en
  T_Flip_Flop t_ff_3 (.clk(out_5), .T(in_2), .Q(out_6), .Qn(out_7));  // open: preset, reset, en
  T_Flip_Flop t_ff_4 (.clk(out_4), .T(in_2), .Q(out_5), .Qn(out_8));  // open: preset, reset, en
  Hex_Digit_Display hex_digit_display_2 (.value({out_7, out_8, out_9, out_10}));  // open: dp

  // Notes on the sheet:
  //   F...0 LOENDUR
endmodule

module _0___9_LOENDUR (
  input  in_1,
  input  in_2,
  output CARRY_OUT
);

  wire not_1_out, not_2_out, t_ff_1_q, t_ff_2_q, t_ff_3_q;
  wire [3:0] t_ff_1_qn;

  T_Flip_Flop t_ff_1 (.clk(in_1), .T(in_2), .Q(t_ff_1_q), .Qn(t_ff_1_qn[0]), .preset(CARRY_OUT));  // open: reset, en
  T_Flip_Flop t_ff_2 (
    .clk(t_ff_1_q), .T(in_2), .Q(t_ff_2_q), .Qn(t_ff_1_qn[1]), .preset(CARRY_OUT));  // open: reset, en
  T_Flip_Flop t_ff_3 (
    .clk(t_ff_2_q), .T(in_2), .Q(t_ff_3_q), .Qn(t_ff_1_qn[2]), .preset(CARRY_OUT));  // open: reset, en
  T_Flip_Flop t_ff_4 (.clk(t_ff_3_q), .T(in_2), .Qn(t_ff_1_qn[3]), .preset(CARRY_OUT));  // open: Q, reset, en
  not not_1 (not_1_out, t_ff_1_qn[0]);
  not not_2 (not_2_out, t_ff_1_qn[2]);
  and and_1 (CARRY_OUT, not_1_out, t_ff_1_qn[1], not_2_out, t_ff_1_qn[3]);
  Hex_Digit_Display hex_digit_display_1 (.value(t_ff_1_qn));  // open: dp

  // Notes on the sheet:
  //   0...9 LOENDUR
endmodule

module KELL (
);

  wire clock_1_out;
  wire [7:0] counter_1_q;

  Clock clock_1 (.out(clock_1_out));
  Counter counter_1 (.Q(counter_1_q), .clk(clock_1_out));  // open: load, D, count, carry, clr
  Hex_Digit_Display hex_digit_display_1 ();  // open: value, dp
  Hex_Digit_Display hex_digit_display_2 (.dp(clock_1_out));  // open: value
  Hex_Digit_Display hex_digit_display_3 ();  // open: value, dp
  Hex_Digit_Display hex_digit_display_4 (.dp(clock_1_out));  // open: value
  Hex_Digit_Display hex_digit_display_5 ();  // open: value, dp
  Hex_Digit_Display hex_digit_display_6 (.value(counter_1_q[3:0]));  // open: dp
  // Pins of 4 and 8 bits meet at counter_1_q
endmodule
