// Logisim project loendurid.circ as structural Verilog: 5 circuits, main circuit main
module main (
  input  in_1,
  input  in_2,
  output out_3,
  output out_4,
  output out_5,
  output out_6,
  output out_7,
  output out_8,
  output out_9,
  output out_10
);

  Hex_Digit_Display hex_digit_display_1 (.value({out_6, out_5, out_4, out_3}));  // open: dp
  T_Flip_Flop t_ff_1 (.clk(in_1), .T(in_2), .Q(out_3), .Qn(out_10));  // open: preset, reset, en
  T_Flip_Flop t_ff_2 (.clk(out_3), .T(in_2), .Q(out_4), .Qn(out_9));  // open: preset, reset, en
  T_Flip_Flop t_ff_3 (.clk(out_5), .T(in_2), .Q(out_6), .Qn(out_7));  // open: preset, reset, en
  T_Flip_Flop t_ff_4 (.clk(out_4), .T(in_2), .Q(out_5), .Qn(out_8));  // open: preset, reset, en
  Hex_Digit_Display hex_digit_display_2 (.value({out_7, out_8, out_9, out_10}));  // open: dp

  // Notes on the sheet:
  //   F...0 LOENDUR
endmodule

module _0___9_LOENDUR (
  input  in_1,
  input  in_2,
  output CARRY_OUT
);

  wire not_1_out, not_2_out, t_ff_1_q, t_ff_2_q, t_ff_3_q;
  wire [3:0] t_ff_1_qn;

  T_Flip_Flop t_ff_1 (.clk(in_1), .T(in_2), .Q(t_ff_1_q), .Qn(t_ff_1_qn[0]), .preset(CARRY_OUT));  // open: reset, en
  T_Flip_Flop t_ff_2 (
    .clk(t_ff_1_q), .T(in_2), .Q(t_ff_2_q), .Qn(t_ff_1_qn[1]), .preset(CARRY_OUT));  // open: reset, en
  T_Flip_Flop t_ff_3 (
    .clk(t_ff_2_q), .T(in_2), .Q(t_ff_3_q), .Qn(t_ff_1_qn[2]), .preset(CARRY_OUT));  // open: reset, en
  T_Flip_Flop t_ff_4 (.clk(t_ff_3_q), .T(in_2), .Qn(t_ff_1_qn[3]), .preset(CARRY_OUT));  // open: Q, reset, en
  not not_1 (not_1_out, t_ff_1_qn[0]);
  not not_2 (not_2_out, t_ff_1_qn[2]);
  and and_1 (CARRY_OUT, not_1_out, t_ff_1_qn[1], not_2_out, t_ff_1_qn[3]);
  Hex_Digit_Display hex_digit_display_1 (.value(t_ff_1_qn));  // open: dp

  // Notes on the sheet:
  //   Kodus teha loendur A-F-ni
  //   0...9 LOENDUR
endmodule

module KELL (
);

  wire clock_1_out, counter_1_carry, counter_2_carry, counter_3_carry, counter_4_carry, counter_5_carry,
       counter_7_carry, H_out, M_out, or_1_out, or_2_out, or_3_out;
  wire [3:0] counter_1_q, counter_2_q, counter_3_q, counter_4_q, counter_5_q, counter_6_q;

  Clock clock_1 (.out(clock_1_out));
  Button M (.out(M_out));
  Button H (.out(H_out));
  Counter #(.width(4), .max('ha)) counter_1 (
    .Q(counter_1_q), .carry(counter_1_carry), .clk(clock_1_out), .clr(counter_1_carry));  // open: load, D, count
  Counter #(.width(4), .max('h6)) counter_2 (
    .Q(counter_2_q), .carry(counter_2_carry), .clk(counter_1_carry), .clr(counter_2_carry));  // open: load, D, count
  or or_1 (or_1_out, counter_2_carry, M_out);
  Counter #(.width(4), .max('h6)) counter_3 (
    .Q(counter_3_q), .carry(counter_3_carry), .clk(counter_4_carry), .clr(counter_3_carry));  // open: load, D, count
  Counter #(.width(4), .max('ha)) counter_4 (
    .Q(counter_4_q), .carry(counter_4_carry), .clk(or_1_out), .clr(counter_4_carry));  // open: load, D, count
  Counter #(.width(4), .max('ha)) counter_5 (
    .Q(counter_5_q), .carry(counter_5_carry), .clk(or_3_out), .clr(or_2_out));  // open: load, D, count
  or or_2 (or_2_out, counter_5_carry, counter_7_carry);
  or or_3 (or_3_out, counter_3_carry, H_out);
  Counter #(.width(4), .max('h2)) counter_6 (
    .Q(counter_6_q), .clk(counter_5_carry), .clr(counter_7_carry));  // open: load, D, count, carry
  Counter #(.max('h18)) counter_7 (
    .carry(counter_7_carry), .clk(or_3_out), .clr(counter_7_carry));  // open: load, D, count, Q
  Hex_Digit_Display hex_digit_display_1 (.value(counter_6_q));  // open: dp
  Hex_Digit_Display hex_digit_display_2 (.value(counter_5_q), .dp(clock_1_out));
  Hex_Digit_Display hex_digit_display_3 (.value(counter_3_q));  // open: dp
  Hex_Digit_Display hex_digit_display_4 (.value(counter_2_q));  // open: dp
  Hex_Digit_Display hex_digit_display_5 (.value(counter_4_q), .dp(clock_1_out));
  Hex_Digit_Display hex_digit_display_6 (.value(counter_1_q));  // open: dp
endmodule

module REGISTRID (
  input  in_1,
  input  in_2,
  input  in_3,
  input  in_4,
  input  in_5,
  input  in_6,
  input  in_7,
  input  in_8,
  input  in_9,
  output out_10,
  output out_11,
  output out_12,
  output out_13,
  output out_14,
  output out_15,
  output out_16,
  output out_17,
  output out_18
);

  wire d_ff_1_q, d_ff_6_q, d_ff_7_q;

  D_Flip_Flop d_ff_1 (.clk(in_1), .D(in_3), .Q(d_ff_1_q));  // open: Qn, preset, en, reset
  D_Flip_Flop d_ff_2 (.clk(in_5), .D(in_6), .Q(out_15));  // open: Qn, preset, en, reset
  D_Flip_Flop d_ff_3 (.clk(in_5), .D(in_7), .Q(out_16));  // open: Qn, preset, en, reset
  D_Flip_Flop d_ff_4 (.clk(in_5), .D(in_8), .Q(out_17));  // open: Qn, preset, en, reset
  D_Flip_Flop d_ff_5 (.clk(in_5), .D(in_9), .Q(out_18));  // open: Qn, preset, en, reset
  D_Flip_Flop d_ff_6 (.clk(in_1), .D(d_ff_1_q), .Q(d_ff_6_q));  // open: Qn, preset, en, reset
  D_Flip_Flop d_ff_7 (.clk(in_1), .D(d_ff_6_q), .Q(d_ff_7_q));  // open: Qn, preset, en, reset
  D_Flip_Flop d_ff_8 (.clk(in_1), .D(d_ff_7_q), .Q(out_10));  // open: Qn, preset, en, reset
  D_Flip_Flop d_ff_9 (.clk(in_2), .D(in_4), .Q(out_11));  // open: Qn, preset, en, reset
  D_Flip_Flop d_ff_10 (.clk(in_2), .D(out_11), .Q(out_12));  // open: Qn, preset, en, reset
  D_Flip_Flop d_ff_11 (.clk(in_2), .D(out_12), .Q(out_13));  // open: Qn, preset, en, reset
  D_Flip_Flop d_ff_12 (.clk(in_2), .D(out_13), .Q(out_14));  // open: Qn, preset, en, reset

  // Notes on the sheet:
  //   RÖÖPREGISTER 4BIT 1TAKT
  //   JADAREGISTER 1BIT 4TAKTI
  //   NIHKE (SHIFT) REGISTER
endmodule

module LED_MATRIKS (
  input  [4:0] in_1
);

  wire clock_1_out, clock_2_out;
  wire [4:0] counter_1_q, rom_1_data, shift_register_1_q0, shift_register_1_q1, shift_register_1_q2,
       shift_register_1_q3, shift_register_1_q4, shift_register_1_q5, shift_register_1_q6,
       shift_register_1_q7, shift_register_2_q0, shift_register_2_q1, shift_register_2_q2,
       shift_register_2_q3, shift_register_2_q4, shift_register_2_q5, shift_register_2_q6,
       shift_register_2_q7;

  Shift_Register #(.width(5)) shift_register_1 (
    .in(in_1), .clk(clock_1_out), .q0(shift_register_1_q0), .q1(shift_register_1_q1),
    .q2(shift_register_1_q2), .q3(shift_register_1_q3), .q4(shift_register_1_q4), .q5(shift_register_1_q5),
    .q6(shift_register_1_q6), .q7(shift_register_1_q7));  // open: shift, out, load, clr, d0, d1, d2, d3, d4, d5, d6, d7
  Clock clock_1 (.out(clock_1_out));
  Counter #(.width(5), .max('h15)) counter_1 (.Q(counter_1_q), .clk(clock_2_out));  // open: load, D, count, carry, clr
  DotMatrix #(.matrixcols(8), .matrixrows(5), .dotshape("circle")) dotmatrix_1 (
    .col0(shift_register_1_q7), .col1(shift_register_1_q6), .col2(shift_register_1_q5),
    .col3(shift_register_1_q4), .col4(shift_register_1_q3), .col5(shift_register_1_q2),
    .col6(shift_register_1_q1), .col7(shift_register_1_q0));
  ROM #(.addrWidth(5), .dataWidth(5)) rom_1 (.addr(counter_1_q), .data(rom_1_data));  // open: sel
  Shift_Register #(.width(5)) shift_register_2 (
    .in(rom_1_data), .clk(clock_2_out), .q0(shift_register_2_q0), .q1(shift_register_2_q1),
    .q2(shift_register_2_q2), .q3(shift_register_2_q3), .q4(shift_register_2_q4), .q5(shift_register_2_q5),
    .q6(shift_register_2_q6), .q7(shift_register_2_q7));  // open: shift, out, load, clr, d0, d1, d2, d3, d4, d5, d6, d7
  Clock clock_2 (.out(clock_2_out));
  DotMatrix #(.matrixcols(8), .matrixrows(5), .dotshape("circle")) dotmatrix_2 (
    .col0(shift_register_2_q7), .col1(shift_register_2_q6), .col2(shift_register_2_q5),
    .col3(shift_register_2_q4), .col4(shift_register_2_q3), .col5(shift_register_2_q2),
    .col6(shift_register_2_q1), .col7(shift_register_2_q0));

  // Notes on the sheet:
  //   YT MEHINE 2
  //   SAAB JÄRGI VAADATA
  //   KODUTÖÖ - OMA NIME VÄLJA KUVAMINE
  //   contents of rom_1 (hex, n*v repeats v):
  //   10 1f 10 0 1f 15 11 0 1f 1f 3 0 15 17 15 0 0 15 9 0 16 8 16 0 12 5 16 0 17 15 7
endmodule
